// Logisim project Project1Given.circ as structural Verilog: 4 circuits, main circuit main
module main (
  input  in_1,
  input  in_2,
  input  in_3,
  input  in_4,
  input  Five,
  output N,
  output E,
  output [3:0] out_8
);

  wire fiveseven_1_a, fiveseven_1_b, fiveseven_1_c, fiveseven_1_d, fiveseven_1_e, fiveseven_1_f,
       fiveseven_1_g;

  Compare compare_1 (.X0(1'b1), .X1(1'b0), .X2(1'b1), .Y0(1'b1), .Y1(1'b1), .Y2(1'b1), .N(N), .E(E));
  Gray gray_1 (.B0(1'b1), .B1(1'b0), .B2(1'b1), .B3(1'b1), .G0(out_8[0]), .G1(out_8[1]), .G2(out_8[2]), .G3(out_8[3]));
  FiveSeven fiveseven_1 (
    .V(in_1), .W(in_2), .X(in_3), .Y(in_4), .Z(Five), .A(fiveseven_1_a), .B(fiveseven_1_b),
    .C(fiveseven_1_c), .D(fiveseven_1_d), .E(fiveseven_1_e), .F(fiveseven_1_f), .G(fiveseven_1_g));
  _7_Segment_Display u_7_segment_display_1 (
    .g(fiveseven_1_g), .f(fiveseven_1_f), .a(fiveseven_1_a), .b(fiveseven_1_b), .e(fiveseven_1_e),
    .d(fiveseven_1_d), .c(fiveseven_1_c));  // open: dp
endmodule

module Compare (
  input  X0,
  input  X1,
  input  X2,
  input  Y0,
  input  Y1,
  input  Y2,
  output N,
  output E
);

  wire and_1_out, and_2_out, and_3_out, and_5_out, and_6_out, and_7_out, and_9_out, and_10_out, and_11_out,
       and_13_out, and_14_out, and_15_out, and_17_out, and_18_out, and_19_out, and_21_out, and_22_out,
       and_23_out, and_25_out, and_26_out, and_27_out, not_1_out, not_2_out, not_3_out, not_4_out, not_5_out,
       not_6_out, not_7_out, not_8_out, not_9_out, not_10_out, not_11_out, not_12_out, not_13_out,
       not_14_out, not_15_out, not_16_out, not_17_out, not_18_out, not_19_out, not_20_out, not_21_out,
       not_22_out, not_23_out, not_24_out, not_25_out, not_26_out, not_27_out, not_28_out, or_1_out,
       or_2_out, or_3_out, or_4_out, or_5_out, or_6_out, or_7_out, or_8_out;

  not not_1 (not_1_out, X2);
  not not_2 (not_2_out, Y2);
  not not_3 (not_3_out, X2);
  not not_4 (not_4_out, Y2);
  and and_1 (and_1_out, X2, Y2);
  and and_2 (and_2_out, not_1_out, not_2_out);
  and and_3 (and_3_out, not_3_out, Y2);
  // AND_Gate and_4 has open pins: in0=X2, in1=not_4_out, out=open
  not not_5 (not_5_out, X1);
  not not_6 (not_6_out, Y1);
  not not_7 (not_7_out, X1);
  not not_8 (not_8_out, Y1);
  not not_9 (not_9_out, X1);
  not not_10 (not_10_out, Y1);
  not not_11 (not_11_out, X1);
  not not_12 (not_12_out, Y1);
  and and_5 (and_5_out, X1, and_1_out, Y1);
  and and_6 (and_6_out, not_5_out, and_1_out, not_6_out);
  and and_7 (and_7_out, not_7_out, and_1_out, Y1);
  // AND_Gate and_8 has open pins: in0=X1, in1=and_1_out, in2=not_8_out, out=open
  and and_9 (and_9_out, X1, and_2_out, Y1);
  and and_10 (and_10_out, not_9_out, and_2_out, not_10_out);
  and and_11 (and_11_out, not_11_out, and_2_out, Y1);
  // AND_Gate and_12 has open pins: in0=X1, in1=and_2_out, in2=not_12_out, out=open
  not not_13 (not_13_out, X0);
  not not_14 (not_14_out, Y0);
  not not_15 (not_15_out, X0);
  not not_16 (not_16_out, Y0);
  not not_17 (not_17_out, X0);
  not not_18 (not_18_out, Y0);
  not not_19 (not_19_out, X0);
  not not_20 (not_20_out, Y0);
  not not_21 (not_21_out, X0);
  not not_22 (not_22_out, Y0);
  not not_23 (not_23_out, X0);
  not not_24 (not_24_out, Y0);
  not not_25 (not_25_out, X0);
  not not_26 (not_26_out, Y0);
  not not_27 (not_27_out, X0);
  not not_28 (not_28_out, Y0);
  and and_13 (and_13_out, X0, and_5_out, Y0);
  and and_14 (and_14_out, not_13_out, and_5_out, not_14_out);
  and and_15 (and_15_out, not_15_out, and_5_out, Y0);
  // AND_Gate and_16 has open pins: in0=X0, in1=and_5_out, in2=not_16_out, out=open
  and and_17 (and_17_out, X0, and_6_out, Y0);
  and and_18 (and_18_out, not_17_out, and_6_out, not_18_out);
  and and_19 (and_19_out, not_19_out, and_6_out, Y0);
  // AND_Gate and_20 has open pins: in0=X0, in1=and_6_out, in2=not_20_out, out=open
  and and_21 (and_21_out, X0, and_9_out, Y0);
  and and_22 (and_22_out, not_21_out, and_9_out, not_22_out);
  and and_23 (and_23_out, not_23_out, and_9_out, Y0);
  // AND_Gate and_24 has open pins: in0=X0, in1=and_9_out, in2=not_24_out, out=open
  and and_25 (and_25_out, X0, and_10_out, Y0);
  and and_26 (and_26_out, not_25_out, and_10_out, not_26_out);
  and and_27 (and_27_out, not_27_out, and_10_out, Y0);
  // AND_Gate and_28 has open pins: in0=X0, in1=and_10_out, in2=not_28_out, out=open
  or or_1 (or_1_out, and_13_out, and_14_out);
  or or_2 (or_2_out, and_17_out, and_18_out);
  or or_3 (or_3_out, and_21_out, and_22_out);
  or or_4 (or_4_out, and_25_out, and_26_out);
  or or_5 (or_5_out, and_15_out, and_19_out, and_7_out);
  or or_6 (or_6_out, and_23_out, and_27_out, and_11_out);
  or or_7 (or_7_out, or_1_out, or_2_out);
  or or_8 (or_8_out, or_3_out, or_4_out);
  or or_9 (E, or_7_out, or_8_out);
  or or_10 (N, or_5_out, or_6_out, and_3_out);

  // Other names for the same wires on the sheet: XequalsY = E; XLessThanY = N
endmodule

module Gray (
  input  B0,
  input  B1,
  input  B2,
  input  B3,
  output G0,
  output G1,
  output G2,
  output G3
);
endmodule

module FiveSeven (
  input  V,
  input  W,
  input  X,
  input  Y,
  input  Z,
  output A,
  output B,
  output C,
  output D,
  output E,
  output F,
  output G
);
endmodule
